# Fritzing sketch Stopwatch (saved by Fritzing 0.9.3b)
breadboards: 1

parts:
  Part1 = Arduino Mega ADK (Rev3)
  R1 = Resistor [tolerance=±5% resistance=220 package=THT]
  R2 = Resistor [tolerance=±5% resistance=220 package=THT]
  R3 = Resistor [tolerance=±5% resistance=220 package=THT]
  R4 = Resistor [tolerance=±5% resistance=220 package=THT]
  R5 = Resistor [tolerance=±5% resistance=220 package=THT]
  R6 = Resistor [tolerance=±5% resistance=220 package=THT]
  S1 = Pushbutton [package="[THT]"]
  S2 = Pushbutton [package="[THT]"]
  LED1 = LED - 5mm [color="Green (570nm)" package="5 mm [THT]"]
  LED2 = LED - 5mm [color="Green (570nm)" package="5 mm [THT]"]
  LED3 = LED - 5mm [color="Green (570nm)" package="5 mm [THT]"]
  LED4 = LED - 5mm [color="Green (570nm)" package="5 mm [THT]"]
  LED5 = LED - 5mm [color="Green (570nm)" package="5 mm [THT]"]
  LED6 = LED - 5mm [color="Green (570nm)" package="5 mm [THT]"]
  R7 = Resistor [tolerance=±5% resistance=220 package=THT]
  R8 = Resistor [tolerance=±5% resistance=220 package=THT]
  R9 = Resistor [tolerance=±5% resistance=220 package=THT]
  R10 = Resistor [tolerance=±5% resistance=220 package=THT]
  R11 = Resistor [tolerance=±5% resistance=220 package=THT]
  R12 = Resistor [tolerance=±5% resistance=220 package=THT]
  LED7 = LED - 5mm [color="Red (633nm)" package="5 mm [THT]"]
  LED8 = LED - 5mm [color="Red (633nm)" package="5 mm [THT]"]
  LED9 = LED - 5mm [color="Red (633nm)" package="5 mm [THT]"]
  LED10 = LED - 5mm [color="Red (633nm)" package="5 mm [THT]"]
  LED11 = LED - 5mm [color="Red (633nm)" package="5 mm [THT]"]
  LED12 = LED - 5mm [color="Red (633nm)" package="5 mm [THT]"]
  R13 = Resistor [tolerance=±5% resistance=220 package=THT]
  R14 = Resistor [tolerance=±5% resistance=220 package=THT]

nets:
  N1: Part1.D14/TX3, S2.Pin_3, S2.Pin_4, R14.Pin_1
  N2: Part1.GND, LED1.cathode, LED2.cathode, LED3.cathode, LED4.cathode, LED5.cathode, LED6.cathode, LED7.cathode, LED8.cathode, LED9.cathode, LED10.cathode, LED11.cathode, LED12.cathode, R13.Pin_0, R14.Pin_0
  N3: Part1.D13_PWM, R12.Pin_1
  N4: Part1.D12_PWM, R11.Pin_1
  N5: Part1.D11_PWM, R10.Pin_1
  N6: Part1.D10_PWM, R9.Pin_1
  N7: Part1.D9_PWM, R8.Pin_1
  N8: Part1.D8_PWM, R7.Pin_1
  N9: Part1.5V, S1.Pin_1, S1.Pin_2, S2.Pin_1, S2.Pin_2
  N10: Part1.D1/TX0, R1.Pin_1
  N11: Part1.D2_PWM, R2.Pin_1
  N12: Part1.D3_PWM, R3.Pin_1
  N13: Part1.D4_PWM, R4.Pin_1
  N14: Part1.D5_PWM, R5.Pin_1
  N15: Part1.D6_PWM, R6.Pin_1
  N16: Part1.D7_PWM, S1.Pin_3, S1.Pin_4, R13.Pin_1
  N17: R1.Pin_0, LED1.anode
  N18: R2.Pin_0, LED2.anode
  N19: R3.Pin_0, LED3.anode
  N20: R4.Pin_0, LED4.anode
  N21: R5.Pin_0, LED5.anode
  N22: R6.Pin_0, LED6.anode
  N23: R7.Pin_0, LED7.anode
  N24: R8.Pin_0, LED8.anode
  N25: R9.Pin_0, LED9.anode
  N26: R10.Pin_0, LED10.anode
  N27: R11.Pin_0, LED11.anode
  N28: R12.Pin_0, LED12.anode
